# Fritzing sketch COMPLETO (saved by Fritzing 1.0.4)
breadboards: 1

parts:
  S2 = Pushbutton [package="[THT]"]
  M3 = FireBeetle ESP32-E
  LED1 = smd LED [color="Red (633nm)" package="0603 [SMD]"]
  R1 = Resistor [tolerance=±5% resistance=220 package="0402 [SMD]"]
  Componente2 = HC-SR501 Body Sensor Module
  Componente3 = Breakout Board for Electret Microphone
  Componente4 = Breakout Board for Electret Microphone
  Mod2 = Passive Buzzer
  Mod3 = KY-031 Knock Sensor Module [package="Breakout board"]

nets:
  GND: S2.Pin_1, S2.Pin_2, M3.pin_12, M3.pin_20, LED1.cathode, Componente2.GND, Componente3.GND, Componente4.GND, Mod2.-, Mod3.-
  N1: S2.Pin_3, S2.Pin_4, M3.pin_3
  N2: M3.pin_1, Mod2.S
  N3: M3.pin_2, R1.Pin_1
  N4: M3.pin_5, Componente4.AUD
  N5: M3.pin_9, Componente2.OUT
  N6: M3.pin_14, Componente2.VCC
  VCC: M3.pin_18, Componente3.VCC, Componente4.VCC, Mod2.NC, Mod3.Vin
  N7: M3.pin_22, Componente3.AUD
  N8: M3.pin_34, Mod3.S
  N9: LED1.anode, R1.Pin_0

custom parts:
  FireBeetle ESP32-E: FireBeetle ESP32-E, specially designed for IoT, is an ESP-WROOM-32E-based main controller board with dual-core chips. It supports WiFi and Bluetooth dual-mode communication and features a small size, ultra-low power consumption, on-board charging circuit, and easy-to-use interface, which can be conveniently used for smart home IoT, industrial IoT applications, wearable devices, and so on. You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
  HC-SR501 Body Sensor Module: Pyroelectric Infrared PIR Motion Sensor Detector Module
  KY-031 Knock Sensor Module: KY-031 Knock Sensor module. A vibration sensor that sends a signal when a knock/tap is detected.
