# Fritzing sketch MAGNETIC SENSOR (saved by Fritzing 1.0.4)
circuit board: 8.46667cm x 5.64444cm
breadboards: 1

parts:
  Mod1 = KY-031 Knock Sensor Module [package="Breakout board"]
  M1 = FireBeetle ESP32-E

nets:
  N1: Mod1.S, M1.pin_24
  N2: Mod1.Vin, M1.pin_18
  N3: Mod1.-, M1.pin_12, M1.pin_20

custom parts:
  KY-031 Knock Sensor Module: KY-031 Knock Sensor module. A vibration sensor that sends a signal when a knock/tap is detected.
  FireBeetle ESP32-E: FireBeetle ESP32-E, specially designed for IoT, is an ESP-WROOM-32E-based main controller board with dual-core chips. It supports WiFi and Bluetooth dual-mode communication and features a small size, ultra-low power consumption, on-board charging circuit, and easy-to-use interface, which can be conveniently used for smart home IoT, industrial IoT applications, wearable devices, and so on. You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
