# Fritzing sketch PIR (saved by Fritzing 1.0.4)
circuit board: 8.46667cm x 5.64444cm
breadboards: 1

parts:
  Componente1 = HC-SR501 Body Sensor Module
  M1 = FireBeetle ESP32-E

nets (from the pcb view):
  N1: Componente1.VCC, M1.pin_14
  N2: Componente1.OUT, M1.pin_4
  N3: Componente1.GND, M1.pin_12, M1.pin_20

custom parts:
  HC-SR501 Body Sensor Module: Pyroelectric Infrared PIR Motion Sensor Detector Module
  FireBeetle ESP32-E: FireBeetle ESP32-E, specially designed for IoT, is an ESP-WROOM-32E-based main controller board with dual-core chips. It supports WiFi and Bluetooth dual-mode communication and features a small size, ultra-low power consumption, on-board charging circuit, and easy-to-use interface, which can be conveniently used for smart home IoT, industrial IoT applications, wearable devices, and so on. You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
