# Fritzing sketch buzzer (saved by Fritzing 1.0.4)
breadboards: 1

parts:
  Mod1 = Passive Buzzer
  M1 = FireBeetle ESP32-E

nets:
  N1: Mod1.S, M1.pin_1
  N2: Mod1.NC, M1.pin_14
  N3: Mod1.-, M1.pin_12

custom parts:
  FireBeetle ESP32-E: FireBeetle ESP32-E, specially designed for IoT, is an ESP-WROOM-32E-based main controller board with dual-core chips. It supports WiFi and Bluetooth dual-mode communication and features a small size, ultra-low power consumption, on-board charging circuit, and easy-to-use interface, which can be conveniently used for smart home IoT, industrial IoT applications, wearable devices, and so on. You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
